# Fritzing sketch Programmer (saved by Fritzing 0.9.3b)
breadboards: 1

parts:
  Part1 = Arduino Uno (Rev3)
  Part2 = Bluetooth HC-05 Macho
  R4 = Resistor [tolerance=±5% resistance=10k package=THT]
  R5 = Resistor [tolerance=±5% resistance=10k package=THT]
  R6 = Resistor [tolerance=±5% resistance=10k package=THT]

nets:
  N1: Part1.D9_PWM, Part2.Key
  N2: Part1.D10_PWM/SS, Part2.TXD
  N3: Part1.D11_PWM/MOSI, R4.Pin_0
  5V: Part1.5V, Part2.VCC
  GND: Part1.GND, Part2.GND, R5.Pin_1
  N4: Part2.RXD, R4.Pin_1, R6.Pin_1
  N5: R5.Pin_0, R6.Pin_0
